// Logisim project hw1_1.circ as structural Verilog: 1 circuit, main circuit hw1_1
module hw1_1 (
  input  [15:0] d,
  input  c,
  input  s,
  output [15:0] address
);

  wire nor_1_out, nor_2_out, nor_3_out, nor_4_out, nor_5_out, nor_6_out, nor_7_out, nor_8_out, nor_9_out,
       nor_10_out, nor_11_out, nor_12_out, nor_13_out, nor_14_out, nor_15_out, not_1_out, not_2_out,
       not_3_out, not_4_out, not_5_out, not_6_out, not_7_out, not_8_out, not_9_out, xnor_1_out, xnor_2_out,
       xnor_3_out, xnor_4_out, xnor_5_out, xnor_6_out, xnor_7_out, xnor_8_out, xnor_9_out, xnor_10_out,
       xnor_11_out, xnor_12_out, xnor_13_out, xnor_14_out, xnor_15_out, xnor_16_out, xnor_17_out,
       xnor_18_out, xnor_19_out, xnor_20_out, xnor_21_out, xnor_22_out, xnor_23_out, xnor_24_out,
       xnor_25_out, xnor_26_out, xnor_27_out, xnor_28_out, xnor_29_out, xnor_30_out, xnor_31_out;

  xnor xnor_1 (xnor_1_out, s, d[14]);
  xnor xnor_2 (xnor_2_out, s, d[13]);
  xnor xnor_3 (xnor_3_out, s, d[12]);
  xnor xnor_4 (xnor_4_out, s, d[11]);
  xnor xnor_5 (xnor_5_out, s, d[10]);
  xnor xnor_6 (xnor_6_out, s, d[9]);
  xnor xnor_7 (xnor_7_out, s, d[8]);
  xnor xnor_8 (xnor_8_out, s, d[7]);
  xnor xnor_9 (xnor_9_out, s, d[6]);
  xnor xnor_10 (xnor_10_out, s, d[5]);
  xnor xnor_11 (xnor_11_out, s, d[4]);
  xnor xnor_12 (xnor_12_out, s, d[3]);
  xnor xnor_13 (xnor_13_out, s, d[2]);
  xnor xnor_14 (xnor_14_out, s, d[1]);
  xnor xnor_15 (xnor_15_out, s, d[0]);
  not not_1 (not_1_out, c);
  not not_2 (not_2_out, c);
  not not_3 (not_3_out, nor_1_out);
  nor nor_1 (nor_1_out, xnor_9_out, xnor_10_out, xnor_11_out, xnor_12_out, xnor_13_out, xnor_14_out, xnor_15_out, not_1_out);
  nor nor_2 (nor_2_out, not_2_out, xnor_15_out);
  nor nor_3 (nor_3_out, xnor_4_out, xnor_5_out, xnor_6_out, xnor_7_out, xnor_8_out, not_3_out);
  nor nor_4 (nor_4_out, xnor_15_out, xnor_14_out, not_2_out);
  xnor xnor_16 (xnor_16_out, d[1], nor_2_out);
  xnor xnor_17 (xnor_17_out, c, d[0]);
  not not_4 (not_4_out, nor_1_out);
  not not_5 (not_5_out, nor_4_out);
  not not_6 (not_6_out, nor_3_out);
  nor nor_5 (nor_5_out, not_4_out, xnor_8_out);
  nor nor_6 (nor_6_out, not_5_out, xnor_13_out);
  nor nor_7 (nor_7_out, xnor_1_out, xnor_2_out, xnor_3_out, not_6_out);
  nor nor_8 (nor_8_out, xnor_8_out, xnor_7_out, not_4_out);
  xnor xnor_18 (xnor_18_out, d[8], nor_5_out);
  xnor xnor_19 (xnor_19_out, nor_1_out, d[7]);
  nor nor_9 (nor_9_out, xnor_13_out, xnor_12_out, not_5_out);
  xnor xnor_20 (xnor_20_out, d[3], nor_6_out);
  xnor xnor_21 (xnor_21_out, nor_4_out, d[2]);
  not not_7 (not_7_out, nor_3_out);
  not not_8 (not_8_out, nor_8_out);
  not not_9 (not_9_out, nor_9_out);
  nor nor_10 (nor_10_out, not_7_out, xnor_3_out);
  nor nor_11 (nor_11_out, not_8_out, xnor_6_out);
  nor nor_12 (nor_12_out, not_9_out, xnor_11_out);
  nor nor_13 (nor_13_out, xnor_3_out, xnor_2_out, not_7_out);
  xnor xnor_22 (xnor_22_out, d[13], nor_10_out);
  xnor xnor_23 (xnor_23_out, nor_3_out, d[12]);
  nor nor_14 (nor_14_out, xnor_6_out, xnor_5_out, not_8_out);
  xnor xnor_24 (xnor_24_out, d[10], nor_11_out);
  xnor xnor_25 (xnor_25_out, nor_8_out, d[9]);
  nor nor_15 (nor_15_out, xnor_11_out, xnor_10_out, not_9_out);
  xnor xnor_26 (xnor_26_out, d[5], nor_12_out);
  xnor xnor_27 (xnor_27_out, nor_9_out, d[4]);
  xnor xnor_28 (xnor_28_out, d[15], nor_7_out);
  not not_10 (address[15], xnor_28_out);
  not not_11 (address[14], xnor_29_out);
  xnor xnor_29 (xnor_29_out, d[14], nor_13_out);
  not not_12 (address[13], xnor_22_out);
  not not_13 (address[12], xnor_23_out);
  not not_14 (address[11], xnor_30_out);
  xnor xnor_30 (xnor_30_out, d[11], nor_14_out);
  not not_15 (address[10], xnor_24_out);
  not not_16 (address[9], xnor_25_out);
  not not_17 (address[8], xnor_18_out);
  not not_18 (address[7], xnor_19_out);
  not not_19 (address[6], xnor_31_out);
  xnor xnor_31 (xnor_31_out, d[6], nor_15_out);
  not not_20 (address[5], xnor_26_out);
  not not_21 (address[4], xnor_27_out);
  not not_22 (address[3], xnor_20_out);
  not not_23 (address[2], xnor_21_out);
  not not_24 (address[1], xnor_16_out);
  not not_25 (address[0], xnor_17_out);
endmodule
